# Fritzing sketch SmartColors! V3 (saved by Fritzing 0.9.3b)

parts:
  Microcontrolador_Samd21 = sparkfun-samd21-mini-breakout
  Pantalla_OLED = OLED Monochrome 128x64 0.96 inch [part_number=326]
  Flora_color_sensor = Flora TCS34725 Color Sensor
  Bateria = LIPO-110mAh [package=lipo-110]
  Switch_alimentación = Toggle Switch [package=THT]
  Switch_2 = Pushbutton [package="[THT]"]
  Switch_1 = Pushbutton [package="[THT]"]

nets:
  N1: Microcontrolador_Samd21.D4, Switch_1.Pin_1
  N2: Microcontrolador_Samd21.D2, Switch_2.Pin_3
  N3: Microcontrolador_Samd21.VIN, Switch_alimentación.L2, Switch_2.Pin_1, Switch_1.Pin_3, Switch_1.Pin_4
  GND: Microcontrolador_Samd21.GND, Pantalla_OLED.VIN, Pantalla_OLED.GND, Flora_color_sensor.GND, Bateria.-
  3.3V: Microcontrolador_Samd21.3.3V, Pantalla_OLED.CS, Pantalla_OLED.3.3V, Flora_color_sensor.3.3V
  N4: Microcontrolador_Samd21.SDA, Pantalla_OLED.MOSI_SDA, Flora_color_sensor.SDA
  N5: Microcontrolador_Samd21.SCL, Pantalla_OLED.SCLK_SCK, Flora_color_sensor.SCL, Flora_color_sensor.SCL_3V
  N6: Bateria.+, Switch_alimentación.COM

notes:
  Escaner de color TCS34725.
  Sparkfun SamD21 mini breakout .
  Pantalla OLED I2C 128x64.

custom parts:
  OLED Monochrome 128x64 0.96 inch: These displays are small, only about 1" diameter, but very readable due to the high contrast of an OLED display. This display is made of 128x64 individual white OLED pixels, each one is turned on or off by the controller chip. Because the display makes its own light, no backlight is required. This reduces the power required to run the OLED and is why the display has such high contrast; we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
  Flora TCS34725 Color Sensor: Your electronics can now see in dazzling color with this lovely color light sensor. We found the best color sensor on the market, the TCS34725, which has RGB and Clear light sensing elements. An IR blocking filter, integrated on-chip and localized to the color sensing photodiodes, minimizes the IR spectral component of the incoming light and allows color measurements to be made accurately. The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
